// Logisim project BES8CPU.circ as structural Verilog: 13 circuits, main circuit main
module main (
  input  Enable,
  input  Cls
);

  wire clock_1_out, ports_1_enable_port_1, ports_1_enable_video, rgb_video_1_p1, rgb_video_1_p2,
       rgb_video_1_p3;
  wire [6:0] bit_extender_1_out;
  wire [7:0] rgb_video_1_p4, rgb_video_1_p5, rgb_video_1_p6;
  wire [15:0] cpu_1_port_addr, cpu_1_port_data_bus_out, ports_1_dataout_port_1, ports_1_dataout_video,
       ports_1_port_data_bus_out, pull_resistor_1_node, video_1_video_data_out;
  wire [19:0] cpu_1_addr_bus_out, rom_1_data;

  Clock clock_1 (.out(clock_1_out));
  ROM #(.addrWidth(20), .dataWidth(20)) rom_1 (.addr(cpu_1_addr_bus_out), .data(rom_1_data));
  Ports ports_1 (
    .Port_Addr_Bus_in(cpu_1_port_addr), .Port_Data_Bus_In(cpu_1_port_data_bus_out),
    .Port_Data_Bus_Out(ports_1_port_data_bus_out), .Enable_Video(ports_1_enable_video),
    .Dataout_Video(ports_1_dataout_video), .DataIn_Video(video_1_video_data_out),
    .Enable_Port_1(ports_1_enable_port_1), .DataOut_Port_1(ports_1_dataout_port_1),
    .DataIn_Port_1(pull_resistor_1_node));  // open: Enable_Port_2, DataOut_Port_2, DataIn_Port_2, Enable_Port_3, DataOut_Port_3, DataIn_Port_3, Enable_Port_4, DataOut_Port_4, DataIn_Port_4
  Pull_Resistor pull_resistor_1 (.node(pull_resistor_1_node));
  CPU cpu_1 (
    .Data_Bus(rom_1_data), .Enable(Enable), .CLK(clock_1_out), .CLS(Cls), .Port_Addr(cpu_1_port_addr),
    .Port_Data_Bus_Out(cpu_1_port_data_bus_out), .Port_Data_Bus_In(ports_1_port_data_bus_out),
    .Addr_Bus_Out(cpu_1_addr_bus_out));  // open: Data_Bus_Out
  // RGB_Video #(.cursor("No Cursor"), .height(256), .scale(1), .width(256)) rgb_video_1: pin names not known; wires that end beside it: rgb_video_1_p1, rgb_video_1_p2, rgb_video_1_p3, rgb_video_1_p4, rgb_video_1_p5, rgb_video_1_p6
  Video video_1 (
    .Enable_Video(ports_1_enable_video), .Video_Data_In(ports_1_dataout_video),
    .Video_Data_Out(video_1_video_data_out), .CLK(clock_1_out), .CLS(Cls), .Video_Reset(rgb_video_1_p1),
    .Video_CLK(rgb_video_1_p2), .Video_Write_Enable(rgb_video_1_p3), .Video_Cursor_X(rgb_video_1_p4),
    .Video_Cursor_Y(rgb_video_1_p5), .Video_Color_Data(rgb_video_1_p6));
  Bit_Extender #(.in_width(16), .out_width(7), .\type ("zero")) bit_extender_1 (
    .in(ports_1_dataout_port_1), .out(bit_extender_1_out));
  TTY tty_1 (.data(bit_extender_1_out), .clk(clock_1_out), .we(ports_1_enable_port_1), .clr(Cls));

  // Notes on the sheet:
  //   contents of rom_1 (hex, n*v repeats v):
  //   20f 0 ffff 10f 37010 5555
endmodule

module CPU (
  input  [15:0] Port_Data_Bus_In,
  input  [19:0] Data_Bus,
  input  Enable,
  input  CLK,
  input  CLS,
  output [15:0] Port_Addr,
  output [15:0] Port_Data_Bus_Out,
  output [19:0] Addr_Bus_Out,
  output [15:0] Data_Bus_Out
);

  wire decoding_logic_1_enablebuffer, decoding_logic_1_inc_reg_32, decoding_logic_1_mov_reg_16,
       decoding_logic_1_output_ram, decoding_logic_1_read_ram, decoding_logic_1_reg_enable,
       decoding_logic_1_set_addr_ram, decoding_logic_1_skack_pop_ram, decoding_logic_1_skack_push_ram,
       decoding_logic_1_write_ram, not_1_out;
  wire [5:0] decoding_logic_1_reg_identifier;
  wire [15:0] allregs16_1_mb_reg_out, bit_extender_1_out, buffer_1_out, decoding_logic_1_immdataout;
  wire [31:0] allregs20_1_pc_out, allregs20_1_sp_out;

  Bit_Extender #(.in_width(20), .\type ("zero")) bit_extender_1 (.in(Data_Bus), .out(bit_extender_1_out));
  assign Port_Data_Bus_Out = not_1_out ? bit_extender_1_out : 16'bz;  // Controlled_Buffer controlled_buffer_1
  not not_1 (not_1_out, decoding_logic_1_enablebuffer);
  assign Port_Data_Bus_Out = decoding_logic_1_enablebuffer ? decoding_logic_1_immdataout : 16'bz;  // Controlled_Buffer controlled_buffer_2
  Decoding_Logic decoding_logic_1 (
    .CLS(CLS), .CLK(CLK), .Enable(Enable), .Data_Bus_In(Data_Bus),
    .EnableBuffer(decoding_logic_1_enablebuffer), .ImmDataOut(decoding_logic_1_immdataout),
    .Reg_identifier(decoding_logic_1_reg_identifier), .Reg_Enable(decoding_logic_1_reg_enable),
    .Mov_Reg_16(decoding_logic_1_mov_reg_16), .Inc_Reg_32(decoding_logic_1_inc_reg_32),
    .Write_Ram(decoding_logic_1_write_ram), .Read_Ram(decoding_logic_1_read_ram),
    .Output_Ram(decoding_logic_1_output_ram), .Set_Addr_Ram(decoding_logic_1_set_addr_ram),
    .Skack_Pop_Ram(decoding_logic_1_skack_pop_ram), .Skack_Push_Ram(decoding_logic_1_skack_push_ram));  // open: Inc_Reg_16, Dec_Reg_16, Mov_Reg_32, Dec_Reg_32, Ports_Data_Out, Ports_Data_In
  assign buffer_1_out = Port_Data_Bus_Out;  // Buffer buffer_1, 16 bits wide
  Register #(.width(16)) register_1 (.D(Data_Bus_Out), .en(1'b1), .Q(Port_Addr), .clk(CLK), .clr(CLS));
  assign Data_Bus_Out = buffer_1_out;  // Buffer buffer_2, 16 bits wide
  AllRegs16 allregs16_1 (
    .Reg_identifier(decoding_logic_1_reg_identifier), .Enable(decoding_logic_1_reg_enable),
    .Data_In_Bus(buffer_1_out), .MOV_Registers(decoding_logic_1_mov_reg_16), .CLK(CLK), .CLS(CLS),
    .MB_reg_out(allregs16_1_mb_reg_out), .Q16(Data_Bus_Out));  // open: OutputReg, DEC, LOAD, PB_Reg_Out, Q8
  AllRegs20 allregs20_1 (
    .Reg_identifier(decoding_logic_1_reg_identifier), .Enable(decoding_logic_1_reg_enable),
    .Data_In_Bus(Data_Bus), .INC(decoding_logic_1_inc_reg_32), .CLK(CLK), .CLS(CLS),
    .SP_out(allregs20_1_sp_out), .PC_out(allregs20_1_pc_out));  // open: OutPut_reg, DEC, LOAD
  Controlled_Buffer #(.width(16)) controlled_buffer_3 (.in(Port_Data_Bus_In));  // open: out, en
  Bit_Extender #(.in_width(32), .out_width(20), .\type ("zero")) bit_extender_2 (
    .in(allregs20_1_pc_out), .out(Addr_Bus_Out));
  RAM_mod ram_mod_1 (
    .Data_Bus_in(Data_Bus), .SP_Reg_32(allregs20_1_sp_out), .MB_Reg_16(allregs16_1_mb_reg_out), .CLK(CLK),
    .Write_Ram(decoding_logic_1_write_ram), .Read_Ram(decoding_logic_1_read_ram),
    .Output_Ram(decoding_logic_1_output_ram), .Set_Addr_Ram(decoding_logic_1_set_addr_ram),
    .Stack_POP_Ram(decoding_logic_1_skack_pop_ram), .Stack_Push_Ram(decoding_logic_1_skack_push_ram),
    .Data_out(buffer_1_out));
endmodule

// Reg16
module Reg16HL (
  input  DEC,
  input  LOAD,
  input  RegisterEnable,
  input  OutputEnabled,
  input  [7:0] IN_L,
  input  [7:0] IN_H,
  input  CLK,
  input  CLS,
  output PCLK,
  output PCLS,
  output PLOAD,
  output PDEC,
  output [7:0] PH,
  output [7:0] PL,
  output Zero,
  output OverFlow,
  output [15:0] Q,
  output [7:0] Q_L,
  output [7:0] Q_H,
  output [15:0] P_Q
);

  wire adder_1_cout, and_1_out, and_2_out, and_3_out, and_4_out, comparator_1_eq, d_ff_1_q, d_ff_2_q,
       not_1_out, not_2_out, or_1_out, or_2_out, or_3_out, subtractor_1_bout;
  wire [15:0] adder_1_out, controlled_buffer_1_out, subtractor_1_out;

  not not_1 (not_1_out, LOAD);
  and and_1 (and_1_out, LOAD, RegisterEnable);
  and and_2 (and_2_out, DEC, not_1_out, RegisterEnable);
  and and_3 (and_3_out, ~DEC, not_1_out, RegisterEnable);  // AND_Gate
  or or_1 (or_1_out, and_3_out, and_2_out);
  not not_2 (not_2_out, or_1_out);
  assign controlled_buffer_1_out = not_2_out ? {IN_H, IN_L} : 16'bz;  // Controlled_Buffer controlled_buffer_1
  Register #(.width(16)) register_1 (.D(controlled_buffer_1_out), .en(or_2_out), .clk(CLK), .Q(P_Q), .clr(CLS));
  or or_2 (or_2_out, or_1_out, and_1_out);
  and and_4 (and_4_out, OutputEnabled, RegisterEnable);
  assign Q = and_4_out ? P_Q : 16'bz;  // Controlled_Buffer controlled_buffer_2
  assign controlled_buffer_1_out = and_3_out ? adder_1_out : 16'bz;  // Controlled_Buffer controlled_buffer_3
  Adder #(.width(16)) adder_1 (.a(P_Q), .b(16'h1), .out(adder_1_out), .cout(adder_1_cout));  // open: cin
  Subtractor #(.width(16)) subtractor_1 (
    .a(P_Q), .b(16'h1), .out(subtractor_1_out), .bout(subtractor_1_bout));  // open: bin
  assign controlled_buffer_1_out = and_2_out ? subtractor_1_out : 16'bz;  // Controlled_Buffer controlled_buffer_4
  D_Flip_Flop d_ff_1 (.D(adder_1_cout), .clk(CLK), .Q(d_ff_1_q));  // open: Qn, preset, reset
  D_Flip_Flop d_ff_2 (.D(subtractor_1_bout), .clk(CLK), .Q(d_ff_2_q));  // open: Qn, preset, reset
  or or_3 (or_3_out, d_ff_1_q, d_ff_2_q);
  Comparator #(.width(16)) comparator_1 (.a({16{1'b0}}), .b(P_Q), .eq(comparator_1_eq));  // open: gt, lt
  assign Zero = and_4_out ? comparator_1_eq : 1'bz;  // Controlled_Buffer controlled_buffer_5
  assign OverFlow = and_4_out ? or_3_out : 1'bz;  // Controlled_Buffer controlled_buffer_6

  assign PCLK = CLK;
  assign PCLS = CLS;
  assign PDEC = DEC;
  assign PH = IN_H;
  assign PL = IN_L;
  assign PLOAD = LOAD;
  assign Q_H = Q[15:8];
  assign Q_L = Q[7:0];
endmodule

// REG20
module REG20HL (
  input  INCorDEC,
  input  LOAD,
  input  Enable,
  input  OutputEnabled,
  input  [9:0] IN_L,
  input  [9:0] IN_H,
  input  CLK,
  input  CLS,
  output PCLK,
  output PCLS,
  output Zero,
  output OverFlow,
  output [15:0] Q_L,
  output [15:0] Q_H,
  output [31:0] Q_X
);

  wire and_1_out, and_2_out, comparator_1_eq, undriven;
  wire [31:0] pull_resistor_1_node;

  and and_1 (and_1_out, LOAD, Enable);
  Counter #(.max('hfffff), .width(20)) counter_1 (
    .clr(CLS), .load(and_1_out), .up(and_2_out), .count(Enable), .clk(CLK), .D({IN_H, IN_L}));  // open: carry, Q
  and and_2 (and_2_out, INCorDEC, Enable);
  Pull_Resistor pull_resistor_1 (.node(pull_resistor_1_node));
  assign Zero = OutputEnabled ? comparator_1_eq : 1'bz;  // Controlled_Buffer controlled_buffer_1
  Comparator #(.width(32)) comparator_1 (
    .a({Q_H, Q_L}), .b(pull_resistor_1_node), .eq(comparator_1_eq));  // open: gt, lt
  assign OverFlow = OutputEnabled ? undriven : 1'bz;  // Controlled_Buffer controlled_buffer_2

  assign PCLK = CLK;
  assign PCLS = CLS;
  assign Q_X = {Q_H, Q_L};
endmodule

module AllRegs16 (
  input  [5:0] Reg_identifier,
  input  Enable,
  input  [15:0] Data_In_Bus,
  input  OutputReg,
  input  DEC,
  input  LOAD,
  input  MOV_Registers,
  input  CLK,
  input  CLS,
  output [15:0] PB_Reg_Out,
  output [15:0] MB_reg_out,
  output [15:0] Q16,
  output [7:0] Q8
);

  wire AX_pclk, AX_pcls, AX_pdec, AX_pload, BX_pclk, BX_pcls, BX_pdec, BX_pload, CX_pclk, CX_pcls, CX_pdec,
       CX_pload, demultiplexer_1_out0, demultiplexer_1_out1, demultiplexer_1_out2, demultiplexer_1_out3,
       demultiplexer_1_out4, demultiplexer_1_out7, demultiplexer_1_out8, demultiplexer_1_out9,
       demultiplexer_1_out14, DX_pclk, DX_pcls, DX_pdec, DX_pload, MB_pclk, MB_pcls, MB_pdec, MB_pload,
       not_1_out, or_1_out, X_pclk, X_pcls, X_pdec, X_pload, Y_pclk, Y_pcls, Y_pdec, Y_pload, ZX_pclk,
       ZX_pcls, ZX_pdec, ZX_pload;
  wire [7:0] AX_ph, AX_pl, BX_ph, BX_pl, controlled_buffer_2_out, controlled_buffer_3_out, CX_ph, CX_pl,
       DX_ph, DX_pl, MB_ph, MB_pl, X_ph, X_pl, Y_ph, Y_pl, ZX_ph, ZX_pl;
  wire [15:0] AX_q, BX_q, controlled_buffer_1_out, CX_q, DX_q, MB_q, multiplexer_1_out, PB_q, X_q, Y_q, ZX_q;

  Demultiplexer #(.enable("true"), .select(4)) demultiplexer_1 (
    .out0(demultiplexer_1_out0), .out1(demultiplexer_1_out1), .out2(demultiplexer_1_out2),
    .out3(demultiplexer_1_out3), .out4(demultiplexer_1_out4), .out7(demultiplexer_1_out7),
    .out8(demultiplexer_1_out8), .out9(demultiplexer_1_out9), .out14(demultiplexer_1_out14), .in(1'b1),
    .sel(Reg_identifier[3:0]), .en(Enable));  // open: out5, out6, out10, out11, out12, out13, out15
  assign controlled_buffer_1_out = not_1_out ? Data_In_Bus : 16'bz;  // Controlled_Buffer controlled_buffer_1
  not not_1 (not_1_out, MOV_Registers);
  or or_1 (or_1_out, LOAD, MOV_Registers);
  assign controlled_buffer_2_out = Reg_identifier[5] ? controlled_buffer_1_out[7:0] : 8'bz;  // Controlled_Buffer controlled_buffer_2
  assign controlled_buffer_3_out = Reg_identifier[4] ? controlled_buffer_1_out[15:8] : 8'bz;  // Controlled_Buffer controlled_buffer_3
  Reg16HL PB (
    .DEC(AX_pdec), .LOAD(AX_pload), .RegisterEnable(demultiplexer_1_out14), .OutputEnabled(OutputReg),
    .IN_L(AX_pl), .IN_H(AX_ph), .CLK(AX_pclk), .CLS(AX_pcls), .Q(PB_q), .P_Q(PB_Reg_Out));  // open: Zero, OverFlow, Q_L, Q_H, PH, PL, PCLK, PCLS, PLOAD, PDEC
  Reg16HL AX (
    .DEC(BX_pdec), .LOAD(BX_pload), .RegisterEnable(OutputReg), .OutputEnabled(demultiplexer_1_out0),
    .IN_L(BX_pl), .IN_H(BX_ph), .CLK(BX_pclk), .CLS(BX_pcls), .Q(AX_q), .PH(AX_ph), .PL(AX_pl),
    .PCLK(AX_pclk), .PCLS(AX_pcls), .PLOAD(AX_pload), .PDEC(AX_pdec));  // open: Zero, OverFlow, Q_L, Q_H, P_Q
  Reg16HL BX (
    .DEC(CX_pdec), .LOAD(CX_pload), .RegisterEnable(OutputReg), .OutputEnabled(demultiplexer_1_out1),
    .IN_L(CX_pl), .IN_H(CX_ph), .CLK(CX_pclk), .CLS(CX_pcls), .Q(BX_q), .PH(BX_ph), .PL(BX_pl),
    .PCLK(BX_pclk), .PCLS(BX_pcls), .PLOAD(BX_pload), .PDEC(BX_pdec));  // open: Zero, OverFlow, Q_L, Q_H, P_Q
  Reg16HL CX (
    .DEC(DX_pdec), .LOAD(DX_pload), .RegisterEnable(OutputReg), .OutputEnabled(demultiplexer_1_out2),
    .IN_L(DX_pl), .IN_H(DX_ph), .CLK(DX_pclk), .CLS(DX_pcls), .Q(CX_q), .PH(CX_ph), .PL(CX_pl),
    .PCLK(CX_pclk), .PCLS(CX_pcls), .PLOAD(CX_pload), .PDEC(CX_pdec));  // open: Zero, OverFlow, Q_L, Q_H, P_Q
  Reg16HL DX (
    .DEC(ZX_pdec), .LOAD(ZX_pload), .RegisterEnable(OutputReg), .OutputEnabled(demultiplexer_1_out3),
    .IN_L(ZX_pl), .IN_H(ZX_ph), .CLK(ZX_pclk), .CLS(ZX_pcls), .Q(DX_q), .PH(DX_ph), .PL(DX_pl),
    .PCLK(DX_pclk), .PCLS(DX_pcls), .PLOAD(DX_pload), .PDEC(DX_pdec));  // open: Zero, OverFlow, Q_L, Q_H, P_Q
  Reg16HL ZX (
    .DEC(MB_pdec), .LOAD(MB_pload), .RegisterEnable(OutputReg), .OutputEnabled(demultiplexer_1_out4),
    .IN_L(MB_pl), .IN_H(MB_ph), .CLK(MB_pclk), .CLS(MB_pcls), .Q(ZX_q), .PH(ZX_ph), .PL(ZX_pl),
    .PCLK(ZX_pclk), .PCLS(ZX_pcls), .PLOAD(ZX_pload), .PDEC(ZX_pdec));  // open: Zero, OverFlow, Q_L, Q_H, P_Q
  Reg16HL MB (
    .DEC(X_pdec), .LOAD(X_pload), .RegisterEnable(OutputReg), .OutputEnabled(demultiplexer_1_out7),
    .IN_L(X_pl), .IN_H(X_ph), .CLK(X_pclk), .CLS(X_pcls), .Q(MB_q), .P_Q(MB_reg_out), .PH(MB_ph), .PL(MB_pl),
    .PCLK(MB_pclk), .PCLS(MB_pcls), .PLOAD(MB_pload), .PDEC(MB_pdec));  // open: Zero, OverFlow, Q_L, Q_H
  Reg16HL X (
    .DEC(Y_pdec), .LOAD(Y_pload), .RegisterEnable(demultiplexer_1_out8), .OutputEnabled(OutputReg),
    .IN_L(Y_pl), .IN_H(Y_ph), .CLK(Y_pclk), .CLS(Y_pcls), .Q(X_q), .PH(X_ph), .PL(X_pl), .PCLK(X_pclk),
    .PCLS(X_pcls), .PLOAD(X_pload), .PDEC(X_pdec));  // open: Zero, OverFlow, Q_L, Q_H, P_Q
  Reg16HL Y (
    .DEC(DEC), .LOAD(or_1_out), .RegisterEnable(demultiplexer_1_out9), .OutputEnabled(OutputReg),
    .IN_L(controlled_buffer_2_out), .IN_H(controlled_buffer_3_out), .CLK(CLK), .CLS(CLS), .Q(Y_q), .PH(Y_ph),
    .PL(Y_pl), .PCLK(Y_pclk), .PCLS(Y_pcls), .PLOAD(Y_pload), .PDEC(Y_pdec));  // open: Zero, OverFlow, Q_L, Q_H, P_Q
  Multiplexer #(.select(4), .width(16)) multiplexer_1 (
    .in0(AX_q), .in1(BX_q), .in2(CX_q), .in3(DX_q), .in4(ZX_q), .in7(MB_q), .in8(X_q), .in9(Y_q),
    .in14(PB_q), .out(multiplexer_1_out), .sel(Reg_identifier[3:0]));  // open: in5, in6, in10, in11, in12, in13, in15
  Register #(.width(16)) register_1 (.D(multiplexer_1_out), .en(OutputReg), .Q(Q16), .clk(CLK), .clr(CLS));
  assign controlled_buffer_1_out = MOV_Registers ? Q16 : 16'bz;  // Controlled_Buffer controlled_buffer_4
  assign Q8 = Reg_identifier[5] ? Q16[7:0] : 8'bz;  // Controlled_Buffer controlled_buffer_5
  assign Q8 = Reg_identifier[4] ? Q16[15:8] : 8'bz;  // Controlled_Buffer controlled_buffer_6
endmodule

module AllRegs20 (
  input  [5:0] Reg_identifier,
  input  Enable,
  input  [19:0] Data_In_Bus,
  input  CLK,
  input  CLS,
  input  OutPut_reg,
  input  INC,
  input  DEC,
  input  LOAD,
  output [31:0] SP_out,
  output [31:0] PC_out
);

  wire demultiplexer_1_out10, demultiplexer_1_out11, or_1_out, PC_pclk, PC_pcls;

  or or_1 (or_1_out, INC, ~DEC);  // OR_Gate
  Demultiplexer #(.select(4)) demultiplexer_1 (
    .out10(demultiplexer_1_out10), .out11(demultiplexer_1_out11), .in(Enable), .sel(Reg_identifier[3:0]));  // open: out0, out1, out2, out3, out4, out5, out6, out7, out8, out9, out12, out13, out14, out15
  REG20HL SP (
    .INCorDEC(or_1_out), .LOAD(LOAD), .Enable(demultiplexer_1_out10), .OutputEnabled(OutPut_reg),
    .IN_L(Data_In_Bus[9:0]), .IN_H(Data_In_Bus[19:10]), .CLK(PC_pclk), .CLS(PC_pcls), .Q_X(SP_out));  // open: Zero, OverFlow, Q_L, Q_H, PCLK, PCLS
  REG20HL PC (
    .INCorDEC(or_1_out), .LOAD(LOAD), .Enable(demultiplexer_1_out11), .OutputEnabled(OutPut_reg),
    .IN_L(Data_In_Bus[9:0]), .IN_H(Data_In_Bus[19:10]), .CLK(CLK), .CLS(CLS), .Q_X(PC_out), .PCLK(PC_pclk),
    .PCLS(PC_pcls));  // open: Zero, OverFlow, Q_L, Q_H
endmodule

module Decoding_Logic (
  input  CLS,
  input  CLK,
  input  Enable,
  input  [19:0] Data_Bus_In,
  output EnableBuffer,
  output [15:0] ImmDataOut,
  output [5:0] Reg_identifier,
  output Reg_Enable,
  output Mov_Reg_16,
  output Inc_Reg_16,
  output Dec_Reg_16,
  output Mov_Reg_32,
  output Inc_Reg_32,
  output Dec_Reg_32,
  output Write_Ram,
  output Read_Ram,
  output Output_Ram,
  output Set_Addr_Ram,
  output Skack_Pop_Ram,
  output Skack_Push_Ram,
  output Ports_Data_Out,
  output Ports_Data_In
);

  wire and_1_out, comparator_1_eq, decoder_1_out0, decoder_1_out1, decoder_1_out15, decoder_2_out0,
       decoder_5_out2, EI, II, not_1_out, not_2_out, not_3_out, or_1_out, RI;
  wire [5:0] register_3_q;
  wire [15:0] bit_extender_1_out;
  wire [19:0] adder_1_out, controlled_buffer_1_out, counter_1_q, register_1_q, rom_1_data;

  Pull_Resistor pull_resistor_1 (.node(EI));
  not not_1 (not_1_out, EI);
  and and_1 (and_1_out, not_1_out, comparator_1_eq);
  Bit_Extender #(.in_width(20), .\type ("zero")) bit_extender_1 (.in(Data_Bus_In), .out(bit_extender_1_out));
  Counter #(.max('hfffff), .width(20)) counter_1 (
    .count(not_2_out), .Q(counter_1_q), .up(not_2_out), .clk(CLK), .clr(EI));  // open: load, D, carry
  Register #(.width(20)) register_1 (.D(Data_Bus_In), .en(and_1_out), .clk(CLK), .Q(register_1_q), .clr(or_1_out));
  or or_1 (or_1_out, CLS, EI);
  Adder #(.width(20)) adder_1 (.a(counter_1_q), .b(register_1_q), .out(adder_1_out));  // open: cin, cout
  not not_2 (not_2_out, comparator_1_eq);
  Comparator #(.width(20)) comparator_1 (.a(register_1_q), .b({20{1'b0}}), .eq(comparator_1_eq));  // open: gt, lt
  Register #(.width(16)) register_2 (.D(bit_extender_1_out), .en(II), .Q(ImmDataOut), .clk(CLK));  // open: clr
  ROM #(.addrWidth(20), .dataWidth(20)) rom_1 (
    .addr(controlled_buffer_1_out), .data({rom_1_data[19], Reg_Enable, rom_1_data[17:0]}));
  assign controlled_buffer_1_out = Enable ? adder_1_out : 20'bz;  // Controlled_Buffer controlled_buffer_1
  Register #(.width(6)) register_3 (.D(Data_Bus_In[5:0]), .en(RI), .Q(register_3_q), .clk(CLK));  // open: clr
  assign Reg_identifier = decoder_5_out2 ? register_3_q : 6'bz;  // Controlled_Buffer controlled_buffer_2
  assign Reg_identifier = not_3_out ? rom_1_data[17:12] : 6'bz;  // Controlled_Buffer controlled_buffer_3
  not not_3 (not_3_out, decoder_5_out2);
  Pull_Resistor pull_resistor_2 (.node(rom_1_data[17:12]));
  Decoder #(.select(4)) decoder_1 (
    .out0(decoder_1_out0), .out1(decoder_1_out1), .out15(decoder_1_out15), .sel(rom_1_data[3:0]), .en(Enable));  // open: out2, out3, out4, out5, out6, out7, out8, out9, out10, out11, out12, out13, out14
  Decoder #(.select(4)) decoder_2 (
    .out0(decoder_2_out0), .out1(Mov_Reg_16), .out5(Inc_Reg_32), .sel(rom_1_data[7:4]), .en(decoder_1_out0));  // open: out2, out3, out4, out6, out7, out8, out9, out10, out11, out12, out13, out14, out15
  Decoder #(.select(4)) decoder_3 (
    .out0(Write_Ram), .out1(Read_Ram), .out2(Output_Ram), .out3(Set_Addr_Ram), .out4(Skack_Pop_Ram),
    .out5(Skack_Push_Ram), .out6(Ports_Data_Out), .out7(Ports_Data_In), .sel(rom_1_data[7:4]),
    .en(decoder_1_out1));  // open: out8, out9, out10, out11, out12, out13, out14, out15
  Decoder #(.select(4)) decoder_4 (
    .out13(II), .out14(RI), .out15(EI), .sel(rom_1_data[7:4]), .en(decoder_1_out15));  // open: out0, out1, out2, out3, out4, out5, out6, out7, out8, out9, out10, out11, out12
  Decoder #(.select(4)) decoder_5 (
    .out0(EnableBuffer), .out2(decoder_5_out2), .sel(rom_1_data[11:8]), .en(Enable));  // open: out1, out3, out4, out5, out6, out7, out8, out9, out10, out11, out12, out13, out14, out15
  Pull_Resistor pull_resistor_3 (.node(Reg_Enable));
  // NoConnect on decoder_2_out0

  // Notes on the sheet:
  //   contents of rom_1 (hex, n*v repeats v):
  //   15*0 45f50 40010 45f50 ff 252*0 45f50 31 45f50 1 45f50 ff 250*0 45f50 ef 45f50 40010 45f50 ff
  //   85498*0 45f50 fdf 45f50 61 45f50 ff 26*0 45f50 fef 45f50 40261 45f50 ff 474*0 45f50 fef 45f50 261
  //   45f50 ff 3610*0 45f50 fdf 45f50
endmodule

module WaitClk (
  input  Enable,
  input  CLK,
  output Output_Data
);

  wire not_1_out;

  D_Flip_Flop d_ff_1 (.D(Enable), .clk(CLK), .Q(Output_Data), .reset(not_1_out));  // open: Qn, preset
  not not_1 (not_1_out, Enable);
endmodule

module RAM_mod (
  input  [19:0] Data_Bus_in,
  input  [31:0] SP_Reg_32,
  input  [15:0] MB_Reg_16,
  input  CLK,
  input  Write_Ram,
  input  Read_Ram,
  input  Output_Ram,
  input  Set_Addr_Ram,
  input  Stack_POP_Ram,
  input  Stack_Push_Ram,
  output [15:0] Data_out
);

  wire and_1_out, bank_controller_1_bank_1, bank_controller_1_bank_2, bank_controller_1_bank_3,
       bank_controller_1_bank_4, banks_2_clk_p, banks_2_rp, banks_2_wp, banks_3_clk_p, banks_3_rp,
       banks_3_wp, banks_4_clk_p, banks_4_rp, banks_4_wp, comparator_1_eq, comparator_1_gt, comparator_2_eq,
       comparator_2_lt, not_1_out, not_2_out, or_1_out, or_2_out, or_3_out, or_4_out, or_5_out;
  wire [15:0] banks_1_output_data, bit_extender_2_out, controlled_buffer_3_out, ram_1_dout;
  wire [19:0] banks_2_addr_p, banks_2_data_p, banks_3_addr_p, banks_3_data_p, banks_4_addr_p, banks_4_data_p,
       bit_extender_1_out, controlled_buffer_1_out, register_1_q;
  wire [31:0] adder_1_out;

  or or_1 (or_1_out, Stack_POP_Ram, Read_Ram);
  or or_2 (or_2_out, Stack_Push_Ram, Write_Ram);
  Register #(.width(20)) register_1 (.D(Data_Bus_in), .en(Set_Addr_Ram), .Q(register_1_q), .clk(CLK));  // open: clr
  or or_3 (or_3_out, Stack_POP_Ram, Stack_Push_Ram);
  Comparator #(.width(20)) comparator_1 (
    .a(register_1_q), .b(20'h32000), .gt(comparator_1_gt), .eq(comparator_1_eq));  // open: lt
  Comparator #(.width(20)) comparator_2 (
    .a(register_1_q), .b(20'h36fff), .eq(comparator_2_eq), .lt(comparator_2_lt));  // open: gt
  assign controlled_buffer_1_out = not_1_out ? register_1_q : 20'bz;  // Controlled_Buffer controlled_buffer_1
  not not_1 (not_1_out, or_3_out);
  Adder #(.width(32)) adder_1 (.a(SP_Reg_32), .b(32'h30200), .out(adder_1_out));  // open: cin, cout
  Bank_Controller bank_controller_1 (
    .MB(MB_Reg_16), .Addr_Enable(and_1_out), .Bank_1(bank_controller_1_bank_1),
    .Bank_2(bank_controller_1_bank_2), .Bank_3(bank_controller_1_bank_3), .Bank_4(bank_controller_1_bank_4));
  or or_4 (or_4_out, comparator_1_gt, comparator_1_eq);
  or or_5 (or_5_out, comparator_2_eq, comparator_2_lt);
  and and_1 (and_1_out, or_5_out, or_4_out);
  Bit_Extender #(.in_width(32), .out_width(20), .\type ("zero")) bit_extender_1 (
    .in(adder_1_out), .out(bit_extender_1_out));
  assign controlled_buffer_1_out = or_3_out ? bit_extender_1_out : 20'bz;  // Controlled_Buffer controlled_buffer_2
  RAM #(.addrWidth(20), .asyncread("true"), .dataWidth(16)) ram_1 (
    .addr(controlled_buffer_1_out), .we(or_2_out), .oe(or_1_out), .clk(CLK), .din(bit_extender_2_out),
    .dout(ram_1_dout));
  Bit_Extender #(.in_width(20), .\type ("zero")) bit_extender_2 (.in(Data_Bus_in), .out(bit_extender_2_out));
  Banks banks_1 (
    .Addr_Bus(banks_2_addr_p), .Data_Bus_in(banks_2_data_p), .CLK(banks_2_clk_p),
    .Enable(bank_controller_1_bank_1), .Write(banks_2_wp), .Read(banks_2_rp),
    .Output_data(banks_1_output_data));  // open: ADDR_P, DATA_P, CLK_P, RP, WP
  Banks banks_2 (
    .Addr_Bus(banks_3_addr_p), .Data_Bus_in(banks_3_data_p), .CLK(banks_3_clk_p),
    .Enable(bank_controller_1_bank_2), .Write(banks_3_wp), .Read(banks_3_rp), .ADDR_P(banks_2_addr_p),
    .DATA_P(banks_2_data_p), .CLK_P(banks_2_clk_p), .RP(banks_2_rp), .WP(banks_2_wp),
    .Output_data(banks_1_output_data));
  Banks banks_3 (
    .Addr_Bus(banks_4_addr_p), .Data_Bus_in(banks_4_data_p), .CLK(banks_4_clk_p),
    .Enable(bank_controller_1_bank_3), .Write(banks_4_wp), .Read(banks_4_rp), .ADDR_P(banks_3_addr_p),
    .DATA_P(banks_3_data_p), .CLK_P(banks_3_clk_p), .RP(banks_3_rp), .WP(banks_3_wp),
    .Output_data(banks_1_output_data));
  Banks banks_4 (
    .Addr_Bus(controlled_buffer_1_out), .Data_Bus_in(Data_Bus_in), .CLK(CLK),
    .Enable(bank_controller_1_bank_4), .Write(or_2_out), .Read(or_1_out), .ADDR_P(banks_4_addr_p),
    .DATA_P(banks_4_data_p), .CLK_P(banks_4_clk_p), .RP(banks_4_rp), .WP(banks_4_wp),
    .Output_data(banks_1_output_data));
  not not_2 (not_2_out, and_1_out);
  assign controlled_buffer_3_out = or_1_out ? ram_1_dout : 16'bz;  // Controlled_Buffer controlled_buffer_3
  Pull_Resistor pull_resistor_1 (.node(controlled_buffer_3_out));
  assign banks_1_output_data = not_2_out ? controlled_buffer_3_out : 16'bz;  // Controlled_Buffer controlled_buffer_4
  assign Data_out = Output_Ram ? banks_1_output_data : 16'bz;  // Controlled_Buffer controlled_buffer_5

  // Notes on the sheet:
  //   Banks are at 0x32000 to 0x36FFF
endmodule

module Banks (
  input  [19:0] Addr_Bus,
  input  [19:0] Data_Bus_in,
  input  CLK,
  input  Enable,
  input  Write,
  input  Read,
  output CLK_P,
  output RP,
  output WP,
  output [19:0] ADDR_P,
  output [19:0] DATA_P,
  output [15:0] Output_data
);

  wire and_1_out, and_2_out;
  wire [14:0] bit_extender_2_out;
  wire [15:0] Banks_dout, bit_extender_1_out;
  wire [19:0] subtractor_1_out;

  Bit_Extender #(.in_width(20)) bit_extender_1 (.in(Data_Bus_in), .out(bit_extender_1_out));
  and and_1 (and_1_out, Enable, Write);
  and and_2 (and_2_out, Enable, Read);
  Subtractor #(.width(20)) subtractor_1 (.a(Addr_Bus), .b(20'h32000), .out(subtractor_1_out));  // open: bin, bout
  RAM #(.addrWidth(15), .asyncread("true"), .dataWidth(16)) Banks (
    .addr(bit_extender_2_out), .we(and_1_out), .oe(and_2_out), .clk(CLK), .din(bit_extender_1_out),
    .dout(Banks_dout));
  Bit_Extender #(.in_width(20), .out_width(15)) bit_extender_2 (.in(subtractor_1_out), .out(bit_extender_2_out));
  assign Output_data = and_2_out ? Banks_dout : 16'bz;  // Controlled_Buffer controlled_buffer_1

  assign ADDR_P = Addr_Bus;
  assign CLK_P = CLK;
  assign DATA_P = Data_Bus_in;
  assign RP = Read;
  assign WP = Write;
endmodule

module Bank_Controller (
  input  Addr_Enable,
  input  [15:0] MB,
  output Bank_1,
  output Bank_2,
  output Bank_3,
  output Bank_4
);

  wire decoder_1_out0, decoder_2_out0, decoder_3_out0;

  Decoder #(.select(4)) decoder_1 (
    .out0(decoder_1_out0), .sel(MB[15:12]), .en(Addr_Enable));  // open: out1, out2, out3, out4, out5, out6, out7, out8, out9, out10, out11, out12, out13, out14, out15
  Decoder #(.select(4)) decoder_2 (
    .out0(decoder_2_out0), .sel(MB[7:4]), .en(decoder_3_out0));  // open: out1, out2, out3, out4, out5, out6, out7, out8, out9, out10, out11, out12, out13, out14, out15
  Decoder #(.select(4)) decoder_3 (
    .out0(decoder_3_out0), .sel(MB[11:8]), .en(decoder_1_out0));  // open: out1, out2, out3, out4, out5, out6, out7, out8, out9, out10, out11, out12, out13, out14, out15
  Decoder #(.select(4)) decoder_4 (
    .out0(Bank_1), .out1(Bank_2), .out2(Bank_3), .out3(Bank_4), .sel(MB[3:0]), .en(decoder_2_out0));  // open: out4, out5, out6, out7, out8, out9, out10, out11, out12, out13, out14, out15
endmodule

module Ports (
  input  [15:0] DataIn_Video,
  input  [15:0] DataIn_Port_1,
  input  [15:0] DataIn_Port_2,
  input  [15:0] DataIn_Port_3,
  input  [15:0] DataIn_Port_4,
  input  [15:0] Port_Addr_Bus_in,
  input  [15:0] Port_Data_Bus_In,
  output Enable_Video,
  output [15:0] Dataout_Video,
  output Enable_Port_1,
  output [15:0] DataOut_Port_1,
  output Enable_Port_2,
  output [15:0] DataOut_Port_2,
  output Enable_Port_3,
  output [15:0] DataOut_Port_3,
  output Enable_Port_4,
  output [15:0] DataOut_Port_4,
  output [15:0] Port_Data_Bus_Out
);

  Comparator #(.width(16)) comparator_1 (.a(Port_Addr_Bus_in), .b(16'h1), .eq(Enable_Video));  // open: gt, lt
  Comparator #(.width(16)) comparator_2 (.a(Port_Addr_Bus_in), .b(16'h2), .eq(Enable_Port_1));  // open: gt, lt
  Comparator #(.width(16)) comparator_3 (.a(Port_Addr_Bus_in), .b(16'h3), .eq(Enable_Port_2));  // open: gt, lt
  Comparator #(.width(16)) comparator_4 (.a(Port_Addr_Bus_in), .b(16'h4), .eq(Enable_Port_3));  // open: gt, lt
  Comparator #(.width(16)) comparator_5 (.a(Port_Addr_Bus_in), .b(16'h5), .eq(Enable_Port_4));  // open: gt, lt

  assign DataIn_Port_2 = DataIn_Port_1;
  assign DataIn_Port_3 = DataIn_Port_1;
  assign DataIn_Port_4 = DataIn_Port_1;
  assign DataIn_Video = DataIn_Port_1;
  assign DataOut_Port_1 = Port_Data_Bus_In;
  assign DataOut_Port_2 = Port_Data_Bus_In;
  assign DataOut_Port_3 = Port_Data_Bus_In;
  assign DataOut_Port_4 = Port_Data_Bus_In;
  assign Dataout_Video = Port_Data_Bus_In;
  assign Port_Data_Bus_Out = DataIn_Port_1;
endmodule

module Video (
  input  Enable_Video,
  input  [15:0] Video_Data_In,
  input  CLK,
  input  CLS,
  output [15:0] Video_Data_Out,
  output Video_Reset,
  output Video_CLK,
  output Video_Write_Enable,
  output [7:0] Video_Cursor_X,
  output [7:0] Video_Cursor_Y,
  output [7:0] Video_Color_Data
);

  wire [15:0] Instr_Register_q;

  Register #(.width(16)) Instr_Register (
    .D(Video_Data_In), .en(Enable_Video), .Q(Instr_Register_q), .clk(CLK), .clr(CLS));

  assign Video_CLK = CLK;
  assign Video_Reset = CLS;
endmodule
